# Fritzing sketch gas-meter (saved by Fritzing 0.9.6b)
circuit board: 5.43956cm x 4.94415cm
breadboards: 1

parts:
  WeMos_D1_Mini1 = WeMos D1 Mini
  S1 = SWITCH-MOMENTARY-2 [package=reed_switch_pth]
  MicroUSB = Adafruit Micro USB Breakout [part_number="Micro USB"]
  R1 = Resistor [tolerance=±5% power=0.25 resistance=1k package=THT]
  JP5 = Header 2 [package=jst-2-smd-vert]
  JP4 = Header 2 [package=jst-2-smd]
  J1 = Camdenboss CTB0158-2 [part_number=CTB0158-2 package=THT]
  S2 = Toggle Switch [package=THT]

nets:
  N1: WeMos_D1_Mini1.3V3, R1.Pin_1
  N2: WeMos_D1_Mini1.5V, S2.COM
  N3: WeMos_D1_Mini1.D5, R1.Pin_0, JP4.2
  N4: WeMos_D1_Mini1.G, MicroUSB.GND, JP4.1, J1.pin1
  N5: S1.1, JP5.1
  N6: S1.2, JP5.2
  N7: MicroUSB.VBUS, S2.L1
  N8: J1.pin2, S2.L2

notes:
  5V 5A DC Input
  Reed switch
  Input val
  JP 2 pin male/female
  1kOhm

custom parts:
  Adafruit Micro USB Breakout: Simple but effective - this breakout board has a USB Micro-B connector, with all 5 pins broken out. Great for pairing with a microcontroller with USB support, or adding USB 5V power to a project. We use a micro-AB connector with through-hole shielding pads for an excellent strong connection - it won't rip off by accident! Comes with one fully assembled and tested micro B breakout PCB and a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
