# Fritzing sketch RGB led strip driver (saved by Fritzing 0.9.6b)
circuit board: 7.74446cm x 4.07528cm
breadboards: 1

parts:
  WeMos_D1_Mini1 = WeMos D1 Mini
  IC1 = ULN2003A [package="DIP16 [THT]"]
  U1 = Voltage Regulator - 5V [package="TO220 [THT]"]
  Power_plug1 = Power plug
  JP1 = Header 4 [package=screwterminal-3.5mm-4_lock]
  JP2 = Header 4 [package=screwterminal-3.5mm-4_lock]

nets:
  N1: WeMos_D1_Mini1.5V, U1.output_voltage
  N2: WeMos_D1_Mini1.D2, IC1.In_3
  N3: WeMos_D1_Mini1.D3, IC1.In_2
  N4: WeMos_D1_Mini1.D4, IC1.In_1
  GND: WeMos_D1_Mini1.G, IC1.0V, U1.GND, Power_plug1.GND
  N5: IC1.COM_-_Common, U1.input_voltage, Power_plug1.VCC, JP1.4, JP2.4
  N6: IC1.Out_3, JP1.3, JP2.3
  N7: IC1.Out_2, JP1.2, JP2.2
  N8: IC1.Out_1, JP1.1, JP2.1

notes:
  12V 5A DC Input
  L7805CV
  12V to 5V
  Voltage Converter
  Simple 5050 RGB led strip
  2 Connectors for both sides of the PCB
