# Fritzing sketch RGB led strip driver2 (saved by Fritzing 0.9.6b)
circuit board: 5.88891cm x 4.14558cm
breadboards: 1
perfboards: 1

parts:
  WeMos_D1_Mini1 = WeMos D1 Mini
  ULN2003A = ULN2003A [package="DIP16 [THT]"]
  Power_plug1 = Power plug
  Mini-360_DC-DC_Buck_converter = Mini-360 DC-DC Buck converter [package=THT]
  JP3 = Header 4 [package=screwterminal-3.5mm-4_lock]
  JP4 = Header 4 [package=screwterminal-3.5mm-4_lock]
  J1 = Camdenboss CTB0158-2 [part_number=CTB0158-2 package=THT]
  S1 = SWITCH_SPDT [package=kps-1290]
  D3 = diac [part_number=DB3 package="300 mil [THT]"]
  D4 = diac [part_number=DB3 package="300 mil [THT]"]

nets (from the pcb view):
  N1: WeMos_D1_Mini1.5V, D3.cathode
  N2: WeMos_D1_Mini1.D5, ULN2003A.In_1
  N3: WeMos_D1_Mini1.D6, ULN2003A.In_3
  N4: WeMos_D1_Mini1.D7, ULN2003A.In_2
  N5: WeMos_D1_Mini1.G, Mini-360_DC-DC_Buck_converter.OUT-
  N6: ULN2003A.0V, Power_plug1.GND, Mini-360_DC-DC_Buck_converter.IN-, J1.pin1
  N7: ULN2003A.COM_-_Common, Mini-360_DC-DC_Buck_converter.IN+, JP3.1, JP4.1, D4.anode
  N8: ULN2003A.Out_3, JP3.2, JP4.2
  N9: ULN2003A.Out_2, JP3.3, JP4.3
  N10: ULN2003A.Out_1, JP3.4, JP4.4
  N11: Power_plug1.VCC, S1.S
  N12: Mini-360_DC-DC_Buck_converter.OUT+, D3.anode
  N13: J1.pin2, S1.O
  N14: S1.P, D4.cathode

notes:
  12V 5A DC Input
  Simple 5050 RGB led strip
  2 Connectors for both sides of the PCB
  12V to 5V DC Buck converter

custom parts:
  Mini-360 DC-DC Buck converter: Mini-360 DC-DC Buck converter. Tiny buck step down voltage converter, input voltage 4.75 to 23V output 1 to 17V adjustable. Available from ebay and the like.
  diac: A standard diac diode
