# Fritzing sketch Livingroom-thermostat-control_nodemcu-32s-wroom (saved by Fritzing 0.9.6b)
breadboards: 1

parts:
  U2 = Nokia 6100 Color LCD [package=nokia6100_lcd]
  Part2 = node32s
  Part3 = Adafruit BME680 [part_number="Adafruit #3660"]
  Part4 = Adafruit Micro USB Breakout [part_number="Adafruit #1833"]

nets:
  GND: U2.RESET, Part2.GND, Part3.GND, Part4.GND
  N1: U2.DIO, Part2.IO17
  N2: U2.SCK, Part2.IO16
  N3: U2.CS, Part2.5V, Part4.VBUS
  3.3V: Part2.3.3V, Part3.VCC
  N4: Part2.IO22, Part3.SDI/SDA
  N5: Part2.IO21, Part3.SCK/SCL

notes:
  Board: NodeMCU-32s
  ESP32-Wroom
  Sensors: BME680
  Display: Nextion NX3224T028 Basic
  Others:
  5V PIN
  TX PIN
  RX PIN
  i2c:
  sda: 21 # SCK - P21
  scl: 22 # SDI - P22
  scan: true
  id: bus_a
  uart:
  id: uart_2
  rx_pin: GPIO16
  tx_pin: GPIO17
  baud_rate: 9600

custom parts:
  Adafruit Micro USB Breakout: Simple but effective - this breakout board has a USB Micro-B connector, with all 5 pins broken out. Great for pairing with a microcontroller with USB support, or adding USB 5V power to a project. We use a micro-AB connector with through-hole shielding pads for an excellent strong connection - it won't rip off by accident! Comes with one fully assembled and tested micro B breakout PCB and a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

// code stored in the sketch: Nextion_display.ino

const int pinButton = 2;
const int pinVCC = 5;
const int pinGND = 7;
const int pinInput = A0;
int potenziometrovalue;
int buttonState;
int old_buttonstate;
int actualpage ;
int pagina;
 
void setup() {
  pinMode(pinButton, INPUT_PULLUP);
  pinMode(pinInput, INPUT);
  pinMode(pinVCC, OUTPUT);
  pinMode(pinGND, OUTPUT);
  
  delay(100);
  digitalWrite(pinVCC,HIGH);
  digitalWrite(pinGND,LOW);
  
  Serial.begin(9600);
  gotopage0();
  actualpage = 0;
}
 
void loop() {
  buttonState = digitalRead(pinButton);
  potenziometrovalue = analogRead(pinInput);
  updatetemp();
  updatetext();
  //sendclick();

  if (buttonState == LOW && old_buttonstate == HIGH){
    switch(actualpage){
      case 0:
        gotopage1();
        actualpage = 1;
      break;
      case 1:
        gotopage0();
        actualpage = 0;
      break;
      
    }
      
    }
  old_buttonstate = buttonState;
  delay(200);
}


void gotopage0(){
    Serial.write("page 0");
    Serial.write(0xFF); // three bytes of 0xFF ... in this case represented as characters 
    Serial.write(0xFF); // three bytes of 0xFF ... in this case represented as characters 
    Serial.write(0xFF); // three bytes of 0xFF ... in this case represented as characters 
}

void gotopage1(){
    Serial.write("page 1");
    Serial.write(0xFF); // three bytes of 0xFF ... in this case represented as characters 
    Serial.write(0xFF); // three bytes of 0xFF ... in this case represented as characters 
    Serial.write(0xFF); // three bytes of 0xFF ... in this case represented as characters 
}

void updatetext(){
    Serial.write("cov temp.val,t0.txt,0");
    Serial.write(0xFF); // three bytes of 0xFF ... in this case represented as characters 
    Serial.write(0xFF); // three bytes of 0xFF ... in this case represented as characters 
    Serial.write(0xFF); // three bytes of 0xFF ... in this case represented as characters 
}

void updatetemp(){
    Serial.write("temp.val=");
    Serial.print(potenziometrovalue);
    Serial.write(0xFF); // three bytes of 0xFF ... in this case represented as characters 
    Serial.write(0xFF); // three bytes of 0xFF ... in this case represented as characters 
    Serial.write(0xFF); // three bytes of 0xFF ... in this case represented as characters 
}

void sendclick(){
  
    Serial.write("click b0,1");
    Serial.write(0xFF); // three bytes of 0xFF ... in this case represented as characters 
    Serial.write(0xFF); // three bytes of 0xFF ... in this case represented as characters 
    Serial.write(0xFF); // three bytes of 0xFF ... in this case represented as characters 
    
    Serial.write("click b0,0");
    Serial.write(0xFF); // three bytes of 0xFF ... in this case represented as characters 
    Serial.write(0xFF); // three bytes of 0xFF ... in this case represented as characters 
    Serial.write(0xFF); // three bytes of 0xFF ... in this case represented as characters 
}
