# Fritzing sketch Livingroom-thermostat-control_wemos-d1-mini (saved by Fritzing 0.9.6b)
breadboards: 1

parts:
  U2 = Nokia 6100 Color LCD [package=nokia6100_lcd]
  Part3 = Adafruit BME680 [part_number="Adafruit #3660"]
  Part4 = Adafruit Micro USB Breakout [part_number="Adafruit #1833"]
  WeMos_D1_Mini1 = WeMos D1 Mini
  D2 = diac [part_number=DB3 package="300 mil [THT]"]
  D3 = diac [part_number=DB3 package="300 mil [THT]"]
  Part5 = I2C Non-Volatile FRAM 32KB
  LED1 = LEDs [package=led10mm]
  RE1 = KY-040 Rotary encoder [package=THT]

nets:
  GND: U2.RESET, Part3.GND, Part4.GND, WeMos_D1_Mini1.G, Part5.GND, LED1.C, RE1.GND
  N1: U2.DIO, WeMos_D1_Mini1.D7
  N2: U2.SCK, WeMos_D1_Mini1.D8
  N3: U2.CS, Part4.VBUS, D3.anode
  VCC: Part3.VCC, D2.cathode, Part5.VCC
  N4: Part3.SCK/SCL, WeMos_D1_Mini1.D1, Part5.SCL
  N5: Part3.SDI/SDA, WeMos_D1_Mini1.D2, Part5.SDA
  3V3: WeMos_D1_Mini1.3V3, D2.anode, RE1.Vcc
  N6: WeMos_D1_Mini1.5V, D3.cathode
  N7: WeMos_D1_Mini1.D3, RE1.CLK
  N8: WeMos_D1_Mini1.D4, LED1.A
  N9: WeMos_D1_Mini1.D5, RE1.SW
  N10: WeMos_D1_Mini1.D6, RE1.DT

notes:
  Board: Wemos D1 mini v2 (ESP8266)
  Sensors: BME680 bsec
  Display: Nextion NX3224T028 Basic
  Others: Adafruit I2C Non-Volatile FRAM 32KB
  5V PIN
  TX PIN
  RX PIN
  uart:
  id: uartbus_nextion
  rx_pin: D8
  tx_pin: D7
  baud_rate: 9600
  i2c:
  - id: i2cbus_bme680
  sda: D2 #SDI
  scl: D1 #SCK
  - id: i2cbus_fram
  sda: D2 #SDA
  scl: D1 #SCL
  Change temp
  Change PRESET MODE
  sensor:
  - platform: rotary_encoder
  name: "Rotary Encoder"
  pin_a: D3 #CLK
  pin_b: D6 #DT
  min_value: 8
  max_value: 35
  binary_sensor:
  - platform: gpio
  pin:
  number: D5 # SW
  mode: INPUT_PULLUP
  inverted: true
  name: "Rotary Button"
  id: preset_mode_switch
  # JOYSTICK
  sensor:
  - platform: adc
  id: joystick_x
  name: "Joystick X axis"
  pin: GPIO33
  internal: True
  attenuation: auto
  update_interval: 500ms
  - platform: adc
  id: joystick_y
  name: "Joystick Y axis"
  pin: GPIO35
  internal: True
  attenuation: 11db
  update_interval: 500ms
  binary_sensor:
  # https://home-assistant-guide.com/guide/how-to-use-a-physical-switch-or-button-in-esphome-with-gpio-binary-sensor/
  - platform: gpio
  id: joystick_click
  pin:
  number: GPIO32
  mode: INPUT_PULLUP
  inverted: True
  name: "Joystick click"
  internal: True
  display:
  ...
  if (id(joystick_x).has_state()) {
  it.printf(127, 70, id(roboto_10), colour_green, TextAlign::BASELINE_RIGHT , "JSX %.1f °", id(joystick_x).state);
  }
  else {
  it.print(127, 70, id(roboto_10), colour_red, TextAlign::TOP_RIGHT ,"NJSX");
  }
  if (id(joystick_y).has_state()) {
  it.printf(127, 80, id(roboto_10), colour_green, TextAlign::BASELINE_RIGHT , "JSY %.1f °", id(joystick_y).state);
  }
  else {
  it.print(127, 80, id(roboto_10), colour_red, TextAlign::TOP_RIGHT ,"NJSY");
  }

custom parts:
  Adafruit Micro USB Breakout: Simple but effective - this breakout board has a USB Micro-B connector, with all 5 pins broken out. Great for pairing with a microcontroller with USB support, or adding USB 5V power to a project. We use a micro-AB connector with through-hole shielding pads for an excellent strong connection - it won't rip off by accident! Comes with one fully assembled and tested micro B breakout PCB and a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
  diac: A standard diac diode
  I2C Non-Volatile FRAM 32KB: With our I2C FRAM breakout board you can add some FRAM storage to your next DIY project. FRAM allows for a lower power usage and a faster write performance. It's excellent for low-power or inconsistent-power datalogging or data buffering where you want to stream data fast while also keeping the data when there's no power. Unlike Flash or EEPROM there's no pages to worry about. Each byte can be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
  KY-040 Rotary encoder: KY-040 Rotary Encoder with switch on breakout borad from AZ Delivery

// code stored in the sketch: Nextion_display.ino

const int pinButton = 2;
const int pinVCC = 5;
const int pinGND = 7;
const int pinInput = A0;
int potenziometrovalue;
int buttonState;
int old_buttonstate;
int actualpage ;
int pagina;
 
void setup() {
  pinMode(pinButton, INPUT_PULLUP);
  pinMode(pinInput, INPUT);
  pinMode(pinVCC, OUTPUT);
  pinMode(pinGND, OUTPUT);
  
  delay(100);
  digitalWrite(pinVCC,HIGH);
  digitalWrite(pinGND,LOW);
  
  Serial.begin(9600);
  gotopage0();
  actualpage = 0;
}
 
void loop() {
  buttonState = digitalRead(pinButton);
  potenziometrovalue = analogRead(pinInput);
  updatetemp();
  updatetext();
  //sendclick();

  if (buttonState == LOW && old_buttonstate == HIGH){
    switch(actualpage){
      case 0:
        gotopage1();
        actualpage = 1;
      break;
      case 1:
        gotopage0();
        actualpage = 0;
      break;
      
    }
      
    }
  old_buttonstate = buttonState;
  delay(200);
}


void gotopage0(){
    Serial.write("page 0");
    Serial.write(0xFF); // three bytes of 0xFF ... in this case represented as characters 
    Serial.write(0xFF); // three bytes of 0xFF ... in this case represented as characters 
    Serial.write(0xFF); // three bytes of 0xFF ... in this case represented as characters 
}

void gotopage1(){
    Serial.write("page 1");
    Serial.write(0xFF); // three bytes of 0xFF ... in this case represented as characters 
    Serial.write(0xFF); // three bytes of 0xFF ... in this case represented as characters 
    Serial.write(0xFF); // three bytes of 0xFF ... in this case represented as characters 
}

void updatetext(){
    Serial.write("cov temp.val,t0.txt,0");
    Serial.write(0xFF); // three bytes of 0xFF ... in this case represented as characters 
    Serial.write(0xFF); // three bytes of 0xFF ... in this case represented as characters 
    Serial.write(0xFF); // three bytes of 0xFF ... in this case represented as characters 
}

void updatetemp(){
    Serial.write("temp.val=");
    Serial.print(potenziometrovalue);
    Serial.write(0xFF); // three bytes of 0xFF ... in this case represented as characters 
    Serial.write(0xFF); // three bytes of 0xFF ... in this case represented as characters 
    Serial.write(0xFF); // three bytes of 0xFF ... in this case represented as characters 
}

void sendclick(){
  
    Serial.write("click b0,1");
    Serial.write(0xFF); // three bytes of 0xFF ... in this case represented as characters 
    Serial.write(0xFF); // three bytes of 0xFF ... in this case represented as characters 
    Serial.write(0xFF); // three bytes of 0xFF ... in this case represented as characters 
    
    Serial.write("click b0,0");
    Serial.write(0xFF); // three bytes of 0xFF ... in this case represented as characters 
    Serial.write(0xFF); // three bytes of 0xFF ... in this case represented as characters 
    Serial.write(0xFF); // three bytes of 0xFF ... in this case represented as characters 
}
