# Fritzing sketch Livingroom-thermostat-relay_wemos-d1-mini-pro (saved by Fritzing 0.9.6b)
breadboards: 1

parts:
  J1 = Screw terminal - 2 pins [package=THT]
  S2 = Pushbutton [package="[SMD]"]
  WeMos_D1_Mini1 = WeMos D1 Mini  # not connected
  1_Channel_Relay1 = 1 Channel Power Relay
  WeMos_D1_Mini_OLED_Shield1 = WeMos D1 Mini OLED Shield  # not connected
  LED1 = smd LED [color="Red (633nm)" package="0805 [SMD]"]
  R1 = Resistor [tolerance=±5% power=0.25 resistance=220 package=THT]
  WeMos_D1_Mini_Relay_Shield_V2 = WeMos D1 Mini Relay Shield V2  # not connected
  WeMos_D1_Mini_OLED_Shield2 = WeMos D1 Mini OLED Shield  # not connected

nets:
  N1: J1.pin1, S2.Pin_3, S2.Pin_4, 1_Channel_Relay1.GND#9, LED1.cathode
  N2: J1.pin2, 1_Channel_Relay1.VCC
  N3: LED1.anode, R1.Pin_1

notes:
  Sensors:
  Others:
  - OLED Wemos OLED Shield 64x48 (SSD1306)
  - 1CH 5V relay
  - push button
  Schematics by Hufnagels

custom parts:
  1 Channel Power Relay: A 1 channel power relay. The module operates at 5V.

// code stored in the sketch: Personal Weather Station.ino
// --Library-- / Bibliotheken
  #include <LiquidCrystal.h>
  #include <DHT.h>
  #include <DHT_U.h>
  
// Sensor DHT-11 (DHT-11 Temperature and Humidity Sensor)
  #define DHTPIN 8
  #define DHTTYPE DHT11

//Declare Sensor

// LCD Display (PIN)(LCD1602 Module)
  LiquidCrystal lcd(12, 11, 5, 4, 3, 2);
  DHT dht(DHTPIN, DHTTYPE);

void setup() {
// Serial Monitor
  Serial.begin(9600);

// Buzzer
  pinMode (10, OUTPUT);  

// LCD Display
  lcd.begin(16, 2);
  lcd.setCursor(7,1);
  dht.begin();
  
// LCD Display (Temp and Humidity)
  lcd.setCursor(0,0);
  lcd.print("TMP:");
  lcd.setCursor(0,1);
  lcd.print("HMD:");
  lcd.setCursor(9,0);
  lcd.print("AIR:");
  lcd.setCursor(9,1);
  lcd.print("UVi:");
  }

void loop() {
  lcd.setCursor(6,1);
  lcd.print("%");
  lcd.setCursor(7,0);
  lcd.print("C");
  lcd.setCursor(6,0);
  lcd.print((char)223);
  lcd.setCursor(15,0);
  lcd.print("%");

// -- Temp and Humidity --
// Temp = Temperature in Fahrenheit and Humid = Humidity
    int f = dht.readHumidity();
    float c = dht.readTemperature(true);
    float ppm = analogRead(A0);
    int perppm = (ppm/300)*100;
    int revper = 100-perppm;
    int uvi = analogRead(A1);
    int temp = ((c-32)*5/9);

  // Sensor Error (For Example No Sensor)
    if (isnan(f) && (c) || isnan(ppm) || isnan(uvi)) {
      lcd.clear();
      lcd.setCursor(4,1);
      lcd.print("|SENSOR|");
      lcd.setCursor(4,0);
      lcd.print("|ERROR |");  
      delay(1000);
      return;
      }

// LCD Display (values)
  lcd.setCursor(4,0);
  lcd.print(temp);
  lcd.setCursor(4,1);
  lcd.print(f);
  lcd.setCursor(13,0);
  lcd.print(revper);
  lcd.setCursor(13,1);
  lcd.print(uvi);

  // Reading Warning
    if (temp >= 38 || temp <= 10 || f >= 85 || revper < 85 || uvi >= 9) {
        digitalWrite (10, HIGH);
        delay (200);
        digitalWrite (10, LOW);
        delay (200);
        digitalWrite (10, HIGH);
        delay (200);
        digitalWrite (10, LOW);
        delay (300000); 
    }
}
